# Fritzing sketch Condutivimetr_Attiny (saved by Fritzing 0.9.10b)
breadboards: 1

parts:
  IC1 = IC, DIP package, 8 pins [chip_label=Att85]
  OLED1 = OLED 128x64 I2C Monochrome Display
  S1 = Pushbutton [package="[THT]"]
  R1 = Resistor [tolerance=±5% power=0.25 resistance=10k package=THT]
  R2 = Resistor [tolerance=±5% power=0.25 resistance=100 package=THT]

nets:
  N1: IC1.pin2, R2.Pin_0
  N2: IC1.pin4, OLED1.GND, R1.Pin_1, R2.Pin_1
  N3: IC1.pin5, OLED1.SDA
  N4: IC1.pin6, S1.Pin_3, S1.Pin_4, R1.Pin_0
  N5: IC1.pin7, OLED1.SCK
  N6: IC1.pin8, OLED1.VDD, S1.Pin_1, S1.Pin_2

notes:
  Eletrodos
